# Fritzing sketch squeak_scheme (saved by Fritzing 0.9.3b)
circuit board: 2.85418cm x 4.64769cm
perfboards: 1

parts:
  C1 = Capacitor [package=cap-pth-small2]
  C2 = Capacitor [package=cap-pth-small2]
  IC = atmega328 [package=dip]
  1702 = Voltage Regulator [package=to-92]
  switch = Toggle Switch [package=THT]
  2N3904 = Voltage Regulator [package=to-92]
  R2 = TRIMPOT [package=trim_pot_pth]
  C4 = Electrolytic Capacitor [capacitance=200µF package="100 mil [THT, electrolytic]"]
  J2 = Screw terminal - 11 pins [package=THT]

nets:
  GND: C1.1, C2.1, IC.GND, 1702.GND, R2.CW, C4.-, J2.Battery_neg, J2.PIR_neg, J2.LED_neg_1, J2.LED_neg_2, J2.Speaker_pos
  N1: C1.2, 1702.IN, switch.COM
  N2: C2.2, IC.VCC, IC.AVCC, IC.AREF, 1702.OUT, 2N3904.OUT, R2.CCW, C4.+, J2.PIR_pos
  N3: IC.D2, J2.PIR_sig
  N4: IC.D11_(PWM), 2N3904.IN
  N5: IC.D13, J2.LED_pos_1, J2.LED_pos_2
  N6: IC.A5, R2.WIPER
  N7: switch.L2, J2.Battery_pos
  N8: 2N3904.GND, J2.Speaker_neg

notes:
  Spk
  -
  +
  s
  ↓
  LED+
  LED-
  PIR:-+s
  bat:+-
  _
  200μF

custom parts:
  Screw terminal - 11 pins: Screw terminal with 11 pins
